// Digital circuit MUX.dig as structural Verilog
module MUX (
  input  D,
  input  C,
  input  B,
  input  A,
  output Y
);

  wire undriven;

  // Not not_1 has open pins: in=undriven, out=open
  Multiplexer #(.Selector_Bits(3)) multiplexer_1 (
    .sel({A, B, C}), .in_0(D), .in_1(1'b0), .in_2(D), .in_3(1'b0), .in_4(1'b1), .in_5(1'b0), .in_6(D),
    .in_7(1'b0), .out(Y));

  // Notes on the sheet:
  //   Use A as the most-significant bit and 
  //   D as the least-significant bit.
  //   Converts between single bits & a 3-bit bus
endmodule

/* Test case:
A B C D Y
0 0 0 0 X
0 0 0 1 1
*/
